# Fritzing sketch Joystick_test (saved by Fritzing 0.9.3b)
breadboards: 1

parts:
  元件2 = Arduino Nano (Rev3.0)
  LCD2 = LCD screen
  R2 = Trimmer Potentiometer [maximum_resistance=10kΩ package=THT]
  元件3 = Thumb Joystick

nets:
  GND: 元件2.GND, LCD2.VSS, LCD2.R/W, LCD2.LED-, R2.leg1, 元件3.GND
  N1: 元件2.D2, 元件3.SEL
  N2: 元件2.D3, LCD2.RS
  N3: 元件2.D4, LCD2.E
  N4: 元件2.D5, LCD2.DB4
  N5: 元件2.D6, LCD2.DB5
  N6: 元件2.D7, LCD2.DB6
  N7: 元件2.D8, LCD2.DB7
  5V: 元件2.5V, LCD2.VDD, LCD2.LED+, R2.leg2, 元件3.VCC
  N8: 元件2.A1, 元件3.VERT
  N9: 元件2.A0, 元件3.HORZ
  N10: LCD2.V0, R2.wiper
