# Fritzing sketch MPU6050_Verification (saved by Fritzing 0.9.3b)
breadboards: 1

parts:
  GY1 = MPU-6050 Board GY-521 [form="♀ (female)" package=THT]
  元件1 = Arduino Nano (Rev3.0)
  LCD1 = LCD screen
  R1 = Trimmer Potentiometer [maximum_resistance=10kΩ package=THT]
  LED1 = LED - 5mm [color="Red (633nm)" package="5 mm [THT]"]
  R2 = Resistor [tolerance=±5% resistance=220 package=THT]

nets:
  5V: GY1.pin1, 元件1.5V, LCD1.VDD, LCD1.LED+, R1.leg2
  GND: GY1.pin2, 元件1.GND, LCD1.VSS, LCD1.R/W, LCD1.LED-, R1.leg1, R2.Pin_0
  N1: GY1.pin3, 元件1.A5
  N2: GY1.pin4, 元件1.A4
  N3: GY1.pin8, 元件1.D2
  N4: 元件1.D3, LCD1.RS
  N5: 元件1.D4, LCD1.E
  N6: 元件1.D5, LCD1.DB4
  N7: 元件1.D6, LCD1.DB5
  N8: 元件1.D7, LCD1.DB6
  N9: 元件1.D8, LCD1.DB7
  N10: 元件1.D13/SCK, LED1.anode
  N11: LCD1.V0, R1.wiper
  N12: LED1.cathode, R2.Pin_1

custom parts:
  MPU-6050 Board GY-521: Acelerometro y Giroscopio MPU-6050 Board GY-521
