# Fritzing sketch nRF24L01_Verification (saved by Fritzing 0.9.3b)
breadboards: 2

parts:
  元件2 = Arduino Nano (Rev3.0)
  元件1 = NRF24L01+ Breakout Board
  元件3 = NRF24L01+ Breakout Board
  元件4 = Arduino Nano (Rev3.0)
  GY3 = MPU-6050 Board GY-521 [form="♀ (female)" package=THT]
  LED3 = LED - 5mm [color="Red (633nm)" package="5 mm [THT]"]
  R5 = Resistor [tolerance=±5% resistance=220 package=THT]
  LCD3 = LCD screen
  R6 = Trimmer Potentiometer [maximum_resistance=10kΩ package=THT]
  LED4 = LED - 5mm [color="Red (633nm)" package="5 mm [THT]"]
  R7 = Resistor [tolerance=±5% resistance=220 package=THT]
  LED5 = LED - 5mm [color="Red (633nm)" package="5 mm [THT]"]
  R8 = Resistor [tolerance=±5% resistance=220 package=THT]

nets:
  GND: 元件2.GND, 元件1.GND, LCD3.VSS, LCD3.R/W, LCD3.LED-, R6.leg1, R8.Pin_0
  N1: 元件2.D2, LED5.anode
  N2: 元件2.D3, LCD3.RS
  N3: 元件2.D4, LCD3.E
  N4: 元件2.D5, LCD3.DB4
  N5: 元件2.D6, LCD3.DB5
  N6: 元件2.D7, LCD3.DB6
  N7: 元件2.D8, LCD3.DB7
  N8: 元件2.D9, 元件1.CE
  N9: 元件2.D10, 元件1.CS
  N10: 元件2.D11/MOSI, 元件1.MOSI
  N11: 元件2.D12/MISO, 元件1.MISO
  5V: 元件2.5V, LCD3.VDD, LCD3.LED+, R6.leg2
  3V3: 元件2.3V3, 元件1.VCC
  N12: 元件2.D13/SCK, 元件1.SCK
  GND_2: 元件3.GND, 元件4.GND, GY3.pin2, R5.Pin_0, R7.Pin_0
  VCC: 元件3.VCC, 元件4.3V3
  N13: 元件3.CE, 元件4.D9
  N14: 元件3.CS, 元件4.D10
  N15: 元件3.SCK, 元件4.D13/SCK
  N16: 元件3.MOSI, 元件4.D11/MOSI
  N17: 元件3.MISO, 元件4.D12/MISO
  N18: 元件4.D2, GY3.pin8
  N19: 元件4.D3, LED3.anode
  N20: 元件4.D4, LED4.anode
  N21: 元件4.5V, GY3.pin1
  N22: 元件4.A5, GY3.pin3
  N23: 元件4.A4, GY3.pin4
  N24: LED3.cathode, R5.Pin_1
  N25: LCD3.V0, R6.wiper
  N26: LED4.cathode, R7.Pin_1
  N27: LED5.cathode, R8.Pin_1

custom parts:
  MPU-6050 Board GY-521: Acelerometro y Giroscopio MPU-6050 Board GY-521
